# Fritzing sketch researchprojectfinal (saved by Fritzing 0.9.4)
breadboards: 1

parts:
  Raspberry_Pi_1 = Raspberry Pi 3 [part_number=RPI-3-V1.2]
  Raspberry_Pi_2 = Raspberry Pi 3 [part_number=RPI-3-V1.2]
  LED1 = LED - 3mm [color="Red (633nm)" package="3 mm [THT]"]
  R1 = Resistor [tolerance=±5% resistance=220 package="0805 [SMD]"]
  U1 = TMP36 [package=to-92]
  ADC1 = MCP3008 [package=dil16]
  Onderdeel1 = Adafruit CCS811 [part_number="Adafruit #3566"]
  SG1 = Buzzer 12mm [package=buzzer-12mm-ns]

nets:
  3V3: Raspberry_Pi_1.3v3, Onderdeel1.VCC
  N1: Raspberry_Pi_1.GPIO2, Onderdeel1.SDA
  N2: Raspberry_Pi_1.GPIO3, Onderdeel1.SCL
  GND: Raspberry_Pi_1.GND, Onderdeel1.GND, SG1.1
  N3: Raspberry_Pi_1.GPIO20, SG1.2
  N4: Raspberry_Pi_1.GPIO25, Onderdeel1.!WAKE
  N5: Raspberry_Pi_2.GPIO10, ADC1.Din
  N6: Raspberry_Pi_2.GPIO9, ADC1.Dout
  N7: Raspberry_Pi_2.GPIO11, ADC1.CLK
  N8: Raspberry_Pi_2.GPIO26, LED1.anode
  GND_2: Raspberry_Pi_2.GND, R1.Pin_0, U1.GND, ADC1.DGND, ADC1.AGND
  N9: Raspberry_Pi_2.GPIO8, ADC1.CS/SHDN
  N10: LED1.cathode, R1.Pin_1
  VCC: U1.VCC, ADC1.VREF, ADC1.VDD
  N11: U1.VOUT, ADC1.CH7

custom parts:
  Adafruit CCS811: Breathe easy - we finally have an I2C VOC/eCO2 sensor in the Adafruit shop! Add air quality monitoring to your project and with an Adafruit CCS811 Air Quality Sensor Breakout. This sensor from AMS is a gas sensor that can detect a wide range of Volatile Organic Compounds (VOCs) and is intended for indoor air quality monitoring. When connected to your microcontroller (running our library code)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
